# Fritzing sketch YB-ESP32-S3-DRV-Fritzing-28BYJ-48(5V) (saved by Fritzing 0.9.5d)
breadboards: 1

parts:
  M1 = YB-ESP32-S3-DRV [part_number=YB-ESP32-S3-DRV package="DIP (Dual Inline) [THT]"]
  MOTOR1 = 28BYJ-48 Stepper Motor [part_number=28BYJ-48-5V]
  C1 = Electrolytic Capacitor [capacitance=100µF package="100 mil [THT, electrolytic]"]

nets:
  N1: M1.5V, M1.+V#20, C1.+
  N2: M1.GND, C1.-
  N3: M1.Y1, MOTOR1.BLUE
  N4: M1.Y2, MOTOR1.PINK
  N5: M1.Y3, MOTOR1.YELLOW
  N6: M1.Y4, MOTOR1.ORANGE
  N7: M1.+V#19, MOTOR1.RED

custom parts:
  YB-ESP32-S3-DRV: Yellobyte YB-ESP32-S3-DRV board, Arduino dev board for driving a wide range of loads including solenoids, stepper motors (e.g. 28BYJ-48), high power LEDs, etc.
  28BYJ-48 Stepper Motor: 28BYJ-48 gear-reduction stepper motor (small)
