# Fritzing sketch YB-ESP32-S3-DRV-Fritzing-Test1 (saved by Fritzing 0.9.5d)
circuit board: 8.46667cm x 5.64444cm
breadboards: 1

parts:
  M1 = YB-ESP32-S3-DRV [part_number=YB-ESP32-S3-DRV package="DIP (Dual Inline) [THT]"]
  R1 = Resistor [tolerance=±5% resistance=220 package=THT]
  LED1 = LED - 5mm [color="Red (633nm)" package="5 mm [THT]"]

nets:
  N1: M1.3V3, LED1.anode
  N2: M1.GPIO10, R1.Pin_0
  N3: M1.GND#14, M1.GND#27, M1.GND#28
  N4: R1.Pin_1, LED1.cathode

custom parts:
  YB-ESP32-S3-DRV: Yellobyte YB-ESP32-S3-DRV board, Arduino dev board for driving a wide range of loads including solenoids, stepper motors (e.g. 28BYJ-48), high power LEDs, etc.
